// Digital circuit four_bit_mux.dig as structural Verilog
module four_bit_mux (
  input  [3:0] a,
  input  [3:0] b,
  input  sel,
  output [3:0] y
);

  Seven_Seg_Hex seven_seg_hex_1 (.d(b), .dp(1'b0));
  Seven_Seg_Hex seven_seg_hex_2 (.d(a), .dp(1'b0));
  // one_bit_mux one_bit_mux_1: pin names not known; wires that end beside it: a[3], b[3], sel, y[3]
  // one_bit_mux one_bit_mux_2: pin names not known; wires that end beside it: a[2], b[2], sel, y[2]
  // one_bit_mux one_bit_mux_3: pin names not known; wires that end beside it: a[1], b[1], sel, y[1]
  // one_bit_mux one_bit_mux_4: pin names not known; wires that end beside it: a[0], b[0], sel, y[0]
  Seven_Seg_Hex seven_seg_hex_3 (.d(y), .dp(1'b0));
  // Pins of 1 and 4 bits meet at a
  // Pins of 1 and 4 bits meet at b
  // Pins of 1 and 4 bits meet at y
endmodule
