// Digital circuit four_bit_reg.dig as structural Verilog
module four_bit_reg (
  input  d,
  input  enable,
  input  clk,
  input  reset,
  output [3:0] q
);

  wire [3:0] four_bit_mux_1_p4;

  // four_bit_mux four_bit_mux_1: pin names not known; wires that end beside it: q, d, enable, four_bit_mux_1_p4
  D_FF_AS d_ff_as_1 (.D(four_bit_mux_1_p4[3]), .C(clk), .Clr(reset), .Q(q[3]));  // open: Set, nQ
  D_FF_AS d_ff_as_2 (.Set(reset), .D(four_bit_mux_1_p4[2]), .C(clk), .Clr(reset), .Q(q[2]));  // open: nQ
  D_FF_AS d_ff_as_3 (.Set(reset), .D(four_bit_mux_1_p4[1]), .C(clk), .Clr(reset), .Q(q[1]));  // open: nQ
  D_FF_AS d_ff_as_4 (.Set(reset), .D(four_bit_mux_1_p4[0]), .C(clk), .Q(q[0]));  // open: Clr, nQ
  // Pins of 1 and 4 bits meet at q
  // also tied to GND on the sheet: reset
endmodule
