// Digital circuit program_ram.dig as structural Verilog
module program_ram (
  input  [1:0] address,
  input  dataln,
  input  write,
  input  clk,
  output dataOut
);

  RAMDualPort ramdualport_1 (.A(address), .Din(dataln), .str(write), .C(clk), .ld(1'b1), .D(dataOut));
  // Pins of 1 and 2 bits meet at address
endmodule
